# Fritzing sketch Car Parking System Diagram (saved by Fritzing 0.9.3b)
breadboards: 1

parts:
  Part1 = Arduino Uno (Rev3)
  J1 = Basic Servo
  M1 = fc-51 [package=THT]
  M2 = fc-51 [package=THT]
  Display1 = LCD screen 16x2 IIC [part_number=101290]
  DHT1 = DHT11 Humitidy and Temperature Sensor
  R1 = Resistor [tolerance=±5% resistance=220 package="0402 [SMD]"]
  LED1 = smd LED [color="Red (633nm)" package="0805 [SMD]"]
  LED2 = Green LED - Rect 5x2x7mm [package="5x2x7 mm [THT]"]
  R2 = Resistor [tolerance=±5% resistance=220 package="2512 [SMD]"]
  R3 = Resistor [tolerance=±5% resistance=220 package="2512 [SMD]"]

nets:
  N1: Part1.A4/SDA, Display1.SDA
  N2: Part1.A5/SCL, Display1.SCL
  N3: Part1.D8, M1.pin1
  N4: Part1.D9_PWM, M2.pin1
  N5: Part1.D10_PWM/SS, DHT1.DATA, R1.Pin_0
  N6: Part1.D11_PWM/MOSI, R2.Pin_1
  N7: Part1.D12/MISO, R3.Pin_1
  N8: Part1.D7, J1.pulse
  VCC: Part1.5V, J1.vcc, M1.pin3, M2.pin3, Display1.VCC, DHT1.VDD, R1.Pin_1
  GND: Part1.GND, J1.gnd, M1.pin2, M2.pin2, Display1.GND, DHT1.GND, LED1.cathode, LED2.cathode
  N9: LED1.anode, R2.Pin_0
  N10: LED2.anode, R3.Pin_0

custom parts:
  LCD screen 16x2 IIC: LCD screen with HD44780 controller enables showing text, symbols, value or anything else that comes from Croduino/Arduino. It is capable of showing 16 symbols in two lines and therefore can be used in many projects that need to send clearly visible and legible output information.. • Color of symbols: White • Backlight: Blue • Dimensions: 80 x 36 x 12 mm • Screen dimensions: 64.5 x 16 mm •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
  DHT11 Humitidy and Temperature Sensor: DHT11 Humidity and Temperature Sensor
  Green LED - Rect 5x2x7mm: A generic rectangular green LED (~1.8V) 5mm x 2mm x 7mm
